// Logisim project AsadVirani(22787)_DanishBadarQureshi(22890)_MarieImplementation.circ as structural Verilog: 2 circuits, main circuit ALU
module ALU (
  input  [11:0] in_1,
  input  [11:0] in_2,
  input  [3:0] in_3,
  output [11:0] out_4
);

  wire [11:0] adder_1_out, multiplier_1_out;

  Adder #(.width(12)) adder_1 (.a(in_1), .b(in_2), .out(adder_1_out));  // open: cin, cout
  Multiplier #(.width(12)) multiplier_1 (.a(in_1), .b(in_2), .out(multiplier_1_out));  // open: cin, cout
  Multiplexer #(.select(4), .width(12), .enable("false")) multiplexer_1 (
    .in1(adder_1_out), .in2(multiplier_1_out), .out(out_4), .sel(in_3));  // open: in0, in3, in4, in5, in6, in7, in8, in9, in10, in11, in12, in13, in14, in15
endmodule

module main (
);

  wire and_1_out, button_1_out, clock_1_out, decoder_1_out0, decoder_1_out1, decoder_1_out2, decoder_1_out3,
       or_1_out, or_2_out, or_3_out;
  wire [7:0] counter_1_q;
  wire [11:0] alu_1_out_4, multiplexer_1_out, ram_2_data, register_1_q;
  wire [15:0] ram_1_data;

  Clock clock_1 (.out(clock_1_out));
  Button button_1 (.out(button_1_out));
  or or_1 (or_1_out, button_1_out, and_1_out);
  Counter counter_1 (.Q(counter_1_q), .clk(clock_1_out), .clr(or_1_out));  // open: load, D, count, carry
  and and_1 (and_1_out, ~clock_1_out, decoder_1_out3);  // AND_Gate
  Multiplexer #(.width(12), .enable("false")) multiplexer_1 (
    .in0(ram_2_data), .in1(alu_1_out_4), .out(multiplexer_1_out), .sel(or_2_out));
  RAM #(.dataWidth(16)) ram_1 (.addr(counter_1_q), .data(ram_1_data));  // open: sel, clk, ld, clr
  or or_2 (or_2_out, decoder_1_out1, decoder_1_out2);
  Decoder #(.select(2), .enable("false")) decoder_1 (
    .out0(decoder_1_out0), .out1(decoder_1_out1), .out2(decoder_1_out2), .out3(decoder_1_out3),
    .sel(ram_1_data[13:12]));
  ALU alu_1 (.in_1(ram_2_data), .in_2(register_1_q), .in_3(ram_1_data[15:12]), .out_4(alu_1_out_4));
  RAM #(.addrWidth(12), .dataWidth(12)) ram_2 (.addr(ram_1_data[11:0]), .data(ram_2_data));  // open: sel, clk, ld, clr
  or or_3 (or_3_out, decoder_1_out2, decoder_1_out1, decoder_1_out0);
  Register #(.width(12)) register_1 (
    .D(multiplexer_1_out), .en(or_3_out), .Q(register_1_q), .clk(clock_1_out), .clr(or_1_out));

  // Notes on the sheet:
  //   Instructions
  //   1. mov 2
  //   2. add 3
  //   3. add 1
  //   4. multiply 2
  //   5. end
  //   Manual reset button
  //   In instruction memory write 0000, 0001, 1002, 1003, 2004, 3000
  //   In data memory write 000, 002, 003, 001, 002
  //   PC
  //   reset with button OR END instruction
  //   only when ADD or MUL opcode is used, then AC updates the result from ALU
  //   AND gate used so that AC resets after displaying previous result
  //   Instruction Memory
  //   using only 2 LSB as only 4 instructions
  //   MUX makes sure to use ALU output and direct LOADing into AC
  //   spit opcode and operand
  //   ALU
  //   Data Memory
  //   ORing between 3 instruction beside halt enable the AC
  //   AC
endmodule
